// Logisim project 01_rs_latch.circ as structural Verilog: 1 circuit, main circuit RS_Latch
module RS_Latch (
  input  R,
  input  S,
  output Q,
  output Q_N
);

  nor nor_1 (Q, R, Q_N);
  nor nor_2 (Q_N, Q, S);
endmodule
