// Logisim project 02_d_latch.circ as structural Verilog: 1 circuit, main circuit D_Latch
module D_Latch (
  input  D,
  input  EN,
  output Q
);

  wire nand_1_out, nand_2_out, nand_3_out, nand_5_out;

  nand nand_1 (nand_1_out, D, D);
  nand nand_2 (nand_2_out, D, EN);
  nand nand_3 (nand_3_out, EN, nand_1_out);
  nand nand_4 (Q, nand_2_out, nand_5_out);
  nand nand_5 (nand_5_out, Q, nand_3_out);

  // Notes on the sheet:
  //   S_n
  //   R_n
endmodule
