// Logisim project 03_d_flip_flop.circ as structural Verilog: 2 circuits, main circuit D_Flip_Flop
module D_Flip_Flop (
  input  D,
  input  CLK,
  output Q
);

  wire d_latch_cell_1_q, not_1_out;

  not not_1 (not_1_out, CLK);
  D_Latch_Cell d_latch_cell_1 (.D(D), .EN(not_1_out), .Q(d_latch_cell_1_q));
  D_Latch_Cell d_latch_cell_2 (.D(d_latch_cell_1_q), .EN(CLK), .Q(Q));

  // Notes on the sheet:
  //   MASTER
  //   SLAVE
endmodule

module D_Latch_Cell (
  input  D,
  input  EN,
  output Q
);

  wire nand_1_out, nand_2_out, nand_3_out, nand_5_out;

  nand nand_1 (nand_1_out, D, D);
  nand nand_2 (nand_2_out, D, EN);
  nand nand_3 (nand_3_out, EN, nand_1_out);
  nand nand_4 (Q, nand_2_out, nand_5_out);
  nand nand_5 (nand_5_out, Q, nand_3_out);

  // Notes on the sheet:
  //   S_n
  //   R_n
endmodule
