// Logisim project 04_jk_flip_flop.circ as structural Verilog: 2 circuits, main circuit JK_Flip_Flop
module JK_Flip_Flop (
  input  J,
  input  K,
  input  CLK,
  output Q
);

  wire CLK_n, d_latch_cell_1_q, K_n, nand_3_out, nand_4_out, nand_5_out, nand_6_out, Q_n_fb;

  nand nand_1 (K_n, K, K);
  nand nand_2 (CLK_n, CLK, CLK);
  nand nand_3 (nand_3_out, J, Q_n_fb);
  nand nand_4 (nand_4_out, K_n, Q);
  nand nand_5 (nand_5_out, J, K_n);
  nand nand_6 (nand_6_out, nand_3_out, nand_4_out, nand_5_out);
  D_Latch_Cell d_latch_cell_1 (.D(nand_6_out), .EN(CLK_n), .Q(d_latch_cell_1_q));
  D_Latch_Cell d_latch_cell_2 (.D(d_latch_cell_1_q), .EN(CLK), .Q(Q));
  nand nand_7 (Q_n_fb, Q, Q);

  // Other names for the same wires on the sheet: Q_fb = Q

  // Notes on the sheet:
  //   D_next
  //   MASTER
  //   SLAVE
endmodule

module D_Latch_Cell (
  input  D,
  input  EN,
  output Q
);

  wire nand_1_out, nand_2_out, nand_3_out, nand_5_out;

  nand nand_1 (nand_1_out, D, D);
  nand nand_2 (nand_2_out, D, EN);
  nand nand_3 (nand_3_out, EN, nand_1_out);
  nand nand_4 (Q, nand_2_out, nand_5_out);
  nand nand_5 (nand_5_out, Q, nand_3_out);

  // Notes on the sheet:
  //   S_n
  //   R_n
endmodule
