// Logisim project 05_d_ff_async_set_clear.circ as structural Verilog: 2 circuits, main circuit D_FF_Async_Set_Clear
module D_FF_Async_Set_Clear (
  input  D,
  input  CLK,
  input  SET,
  input  CLR,
  output Q
);

  wire async_d_latch_cell_1_q, CLK_n, not_1_out, RUN, SET_E;

  not not_1 (not_1_out, CLR);
  not not_2 (CLK_n, CLK);
  nor nor_1 (RUN, SET, CLR);
  and and_1 (SET_E, SET, not_1_out);
  Async_D_Latch_Cell async_d_latch_cell_1 (
    .D(D), .EN(CLK_n), .RUN(RUN), .SET_E(SET_E), .CLR(CLR), .Q(async_d_latch_cell_1_q));
  Async_D_Latch_Cell async_d_latch_cell_2 (
    .D(async_d_latch_cell_1_q), .EN(CLK), .RUN(RUN), .SET_E(SET_E), .CLR(CLR), .Q(Q));

  // Notes on the sheet:
  //   MASTER
  //   SLAVE
endmodule

module Async_D_Latch_Cell (
  input  SET_E,
  input  D,
  input  EN,
  input  RUN,
  input  CLR,
  output Q
);

  wire and_1_out, and_2_out, nand_2_out, nor_1_out, nor_2_out, not_1_out;

  not not_1 (not_1_out, D);
  and and_1 (and_1_out, D, EN, RUN);
  and and_2 (and_2_out, not_1_out, EN, RUN);
  nor nor_1 (nor_1_out, and_1_out, SET_E);
  nor nor_2 (nor_2_out, and_2_out, CLR);
  nand nand_1 (Q, nor_1_out, nand_2_out);
  nand nand_2 (nand_2_out, Q, nor_2_out);

  // Notes on the sheet:
  //   S_n
  //   R_n
endmodule
